# Fritzing sketch Booze Button (saved by Fritzing 0.9.5d)

parts:
  U1 = NodeMCU V1.0
  RE1 = Rotary Encoder [package=THT]
  U2 = NodeMCU V1.0
  Light_Button = Round Pushbutton
  S2 = SWITCH-MOMENTARY-2 [package=tactile-pth]
  BAT1 = Battery Holders [package=battery-aa-panel]
  Part1 = ws2812b [package="smd 2812b"]
  Part2 = ws2812b [package="smd 2812b"]
  BAT2 = Battery Holders [package=battery-aa-panel]

nets:
  N1: U1.D2, Part1.DIN
  N2: U1.D3, S2.1
  N3: U1.D4, Light_Button.leg0
  GND: U1.GND, RE1.EncoderPinC, S2.2, BAT1.-, Part1.VSS
  N4: U1.D5, RE1.EncoderPinA
  N5: U1.D6, RE1.EncoderPinB
  VIN: U1.Vin, BAT1.+, Part1.VDD
  N6: U2.D4, Part2.DIN
  GND_2: U2.GND, Part2.VSS, BAT2.-
  VIN_2: U2.Vin, Part2.VDD, BAT2.+

custom parts:
  NodeMCU V1.0: ESP8266 based NodeMCU
